# Fritzing sketch Head electronics (saved by Fritzing 0.9.6b)
breadboards: 2

parts:
  S1 = Pushbutton [package="[THT]"]
  S2 = Pushbutton [package="[THT]"]
  S3 = Pushbutton [package="[THT]"]
  S4 = Pushbutton [package="[THT]"]
  Part2 = Mini 8x8 LED Matrix Backpack [part_number=870]
  MCU1 = Raspberry Pi Zero
  NEOPIXEL2 = Neopixel Strip -- Black (60/m) [part_number=1461]
  NEOPIXEL3 = Neopixel Strip -- Black (60/m) [part_number=1461]
  Part3 = Adafruit Micro USB Breakout [part_number="Adafruit #1833"]
  SPKR1 = Loudspeaker  # not connected
  MIC1 = Microphone  # not connected
  S5 = Pushbutton [package="[THT]"]
  PART2 = Sound Detector
  Part5 = I2C level shifter bidirectional
  R1 = Resistor [tolerance=±5% power=0.25 resistance=470k package=THT]

nets:
  GND: S1.Pin_1, S1.Pin_2, S2.Pin_1, S2.Pin_2, S3.Pin_1, S3.Pin_2, S4.Pin_1, S4.Pin_2, Part2.GND, MCU1.pin_6, MCU1.pin_34, NEOPIXEL2.GND, NEOPIXEL3.GND, Part3.GND, S5.Pin_1, S5.Pin_2, Part5.GND
  N1: S1.Pin_3, S1.Pin_4, MCU1.pin_3
  N2: S2.Pin_3, S2.Pin_4, MCU1.pin_11
  N3: S3.Pin_3, S3.Pin_4, MCU1.pin_5
  N4: S4.Pin_3, S4.Pin_4, MCU1.pin_7
  N5: Part2.SDA, Part5.HV4
  +5V: Part2.VDD, MCU1.pin_2, MCU1.pin_4, NEOPIXEL2.+5V, NEOPIXEL3.+5V, Part3.VBUS, Part5.HV
  N6: MCU1.pin_1, MCU1.pin_17, Part5.LV
  N7: MCU1.pin_8, Part5.LV1
  N8: MCU1.pin_12, Part5.LV2
  N9: MCU1.pin_13, S5.Pin_3, S5.Pin_4
  N10: MCU1.pin_33, Part5.LV4
  N11: NEOPIXEL2.DI, NEOPIXEL3.DI, Part5.HV2
  N12: PART2.R17#5, R1.Pin_1
  N13: PART2.R17#6, R1.Pin_0

notes:
  USB sound card connects Pi to mic and speaker
  [1.0m]
  [1.0m, 2 wires to disconnect mic]
  [1.5m]
  [0.3m]

custom parts:
  Mini 8x8 LED Matrix Backpack: This 0.8" 8x8 monochrome LED matrix includes a driver chip for simple control via an I2C interface. The backpack features address-selection jumpers so you can connect up to four matrices on a single I2C bus.
  Neopixel Strip -- Black (60/m): Neopixel Strip, Black, 60 pixels per meter.
  Adafruit Micro USB Breakout: Simple but effective - this breakout board has a USB Micro-B connector, with all 5 pins broken out. Great for pairing with a microcontroller with USB support, or adding USB 5V power to a project. We use a micro-AB connector with through-hole shielding pads for an excellent strong connection - it won't rip off by accident! Comes with one fully assembled and tested micro B breakout PCB and a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
  Sound Detector: Electret microphone with multiple outputs. - First output is the actual audio - Second output is the amplitude envelope - Third output is a binary "sound present" indication - high while sound is present, low otherwise. Visit sparkfun.com for more documentations.
